# Fritzing sketch electron-gps (saved by Fritzing 0.9.2b)
breadboards: 1

parts:
  Photon = Photon
  GPS1 = Adafruit Ultimate GPS Breakout

nets:
  N1: Photon.RX, GPS1.TX
  N2: Photon.TX, GPS1.RX
  GND: Photon.GND, GPS1.GND
  VIN: Photon.VIN, GPS1.VIN
  N3: Photon.D1, GPS1.EN
